# Fritzing sketch decoder-display (saved by Fritzing 1.0.4)
breadboards: 1

parts:
  Teensy1 = Teensy 4.1
  OLED3 = OLED 128x64 I2C Monochrome Display VDD-GND
  OLED4 = OLED 128x64 I2C Monochrome Display VDD-GND
  OLED5 = OLED 128x64 I2C Monochrome Display VDD-GND
  Morse_Key = Pushbutton [package=THT]
  R2 = Resistor [tolerance=±5% resistance=47 package="0402 [SMD]"]
  S1 = Pushbutton [package="[THT]"]
  LED1 = smd LED [color="Red (633nm)" package="0603 [SMD]"]
  R3 = Resistor [tolerance=±5% resistance=220 package="0402 [SMD]"]

nets:
  GND: Teensy1.GND, Teensy1.GND2, OLED3.GND, OLED4.GND, OLED5.GND, R2.Pin_1, S1.Pin_3, S1.Pin_4, R3.Pin_1
  N1: Teensy1.D2, Morse_Key.leg1, LED1.cathode, R3.Pin_0
  N2: Teensy1.D10, S1.Pin_1, S1.Pin_2
  N3: Teensy1.A2/D16, OLED4.SCK
  N4: Teensy1.A3/D17, OLED4.SDA
  N5: Teensy1.A4/D18, OLED5.SDA
  N6: Teensy1.A5/D19, OLED5.SCK
  VDD: Teensy1.3V3_LOW, OLED3.VDD, OLED4.VDD, OLED5.VDD, Morse_Key.leg0
  N7: Teensy1.A10/D24, OLED3.SCK
  N8: Teensy1.A11/D25, OLED3.SDA
  N9: R2.Pin_0, LED1.anode

notes:
  GPIO morse code decoder with 3 OLED displays and serial decoder output.
  https://github.com/EnigmaCurry/code-smore

custom parts:
  Teensy 4.1: The Teensy is a complete USB-based microcontoller development system, in a very small footprint, capable of implementing many types of projects. All programming is done via the USB port. No special programmer is needed, only a standard micro-USB cable and a PC or Macintosh with a USB port.
  OLED 128x64 I2C Monochrome Display VDD-GND: OLED 128x64 I2C Monochrome Display. Note: there are two variants of this part, this one is the VDD GND SCK SDA variant. The other is GND VDD SCK SDA. Make sure you select the part that matches your module as using the incorrect part will probably destroy your module! In addition the mounting holes are marked on silkscreen but not by default drilled. If you want drilled mounting holes, copy a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
